# Fritzing sketch digital_input_pullup (saved by Fritzing 0.9.0b)
breadboards: 1

parts:
  Part1 = Arduino Nano (Rev3.0)
  R9 = Resistor [tolerance=±5% resistance=220 package=THT]
  LED1 = LED - 5mm [color="Red (633nm)" package="5 mm [THT]"]
  S2 = Pushbutton [package="[THT]"]

nets:
  N1: Part1.GND, LED1.cathode, S2.Pin_1, S2.Pin_2
  N2: Part1.D12/MISO, S2.Pin_3, S2.Pin_4
  N3: Part1.D13/SCK, R9.Pin_1
  N4: R9.Pin_0, LED1.anode
