# Fritzing sketch analog_input_pwm (saved by Fritzing 0.9.2b)
breadboards: 1

parts:
  Part1 = Arduino Nano (Rev3.0)
  R9 = Resistor [tolerance=±5% resistance=220 package=THT]
  LED1 = LED - 5mm [color="Red (633nm)" package="5 mm [THT]"]
  R11 = Rotary Potentiometer (Small) [maximum_resistance=100kΩ package=THT]

nets:
  N1: Part1.D11/MOSI, R9.Pin_1
  N2: Part1.GND, LED1.cathode, R11.leg2
  N3: Part1.5V, R11.leg1
  N4: Part1.A0, R11.wiper
  N5: R9.Pin_0, LED1.anode
